# Fritzing sketch ESPostifICE (saved by Fritzing 0.9.9b)
breadboards: 1

parts:
  LCD1 = 1_54in tft lcd
  Composant1 = node32s
  R1 = Trimmer Potentiometer [maximum_resistance=10kΩ package=THT]
  S1 = Pushbutton [package="[THT]"]
  S2 = Pushbutton [package="[THT]"]
  S3 = Pushbutton [package="[THT]"]

nets:
  N1: LCD1.pin_1, Composant1.GND, R1.leg1, S1.Pin_3, S1.Pin_4, S2.Pin_3, S2.Pin_4, S3.Pin_3, S3.Pin_4
  N2: LCD1.pin2, LCD1.pin_8, Composant1.3.3V, R1.leg2
  N3: LCD1.pin3, Composant1.IO14
  N4: LCD1.pin4, Composant1.IO13
  N5: LCD1.pin_5, Composant1.IO4
  N6: LCD1.pin_6, Composant1.IO5
  N7: LCD1.pin_7, Composant1.IO15
  N8: Composant1.IO36, R1.wiper
  N9: Composant1.IO39, S1.Pin_1, S1.Pin_2
  N10: Composant1.IO34, S2.Pin_1, S2.Pin_2
  N11: Composant1.IO35, S3.Pin_1, S3.Pin_2

custom parts:
  1_54in tft lcd: This is the DONGKER 1.54'' LCD Display Module, SPI 240x240 1.54'' LCD Display Module ST7789 Driver 240x240 3.3V IPS LCD Display Screen Module. The 1.54" display has 240x240 color pixels.
